# Fritzing sketch GirlWithBalloon (saved by Fritzing 1.0.0rc)
circuit board: 1.6707cm x 1.68832cm
breadboards: 1

parts:
  TINY85 = attiny85 [package=dip]
  Hum = female pin header, 2 pins [form="♀ (female)"]
  R1 = Resistor [tolerance=±5% power=0.25W resistance=1M package=THT]
  B = female pin header, 2 pins [form="♀ (female)"]
  H = female pin header, 2 pins [form="♀ (female)"]
  Bat = female pin header, 2 pins [form="♀ (female)"]
  D1 = female pin header, 1 pin [form="♀ (female)"]
  RST = female pin header, 1 pin [form="♀ (female)"]
  G = female pin header, 1 pin [form="♀ (female)"]

nets:
  N1: TINY85.Pin_1, RST.pin1
  N2: TINY85.Pin_2, H.pin1
  N3: TINY85.Pin_3, B.pin2
  GND: TINY85.Pin_4, Hum.pin2, B.pin1, H.pin2, Bat.pin2, G.pin1
  N4: TINY85.Pin_5, R1.Pin_0
  N5: TINY85.Pin_6, D1.pin1
  N6: TINY85.Pin_7, Hum.pin1, R1.Pin_1
  N7: TINY85.Pin_8, Bat.pin1

notes:
  g
